// Logisim project 16-bit-pipelined-processor.circ as structural Verilog: 9 circuits, main circuit main
module main (
);

  wire alu_1_zero_output, and_1_out, clock_1_out, ex_1_alusrc, ex_1_beq, ex_1_bne, ex_1_extop, ex_1_j,
       ex_1_jr, ex_1_memread, ex_1_memwrite, ex_1_regwrite, hazard_detect_n_forward_1_stall, mem_1_memread,
       mem_1_memwrite, mem_1_regwrite, next_pc_1_pcsrc, not_1_out, or_1_out, RegWrite_q;
  wire [1:0] ex_1_toreg, hazard_detect_n_forward_1_forwarda, hazard_detect_n_forward_1_forwardb,
       main_ctrl_1_regdst, mem_1_toreg;
  wire [2:0] multiplexer_4_out, Rd2_q, Rd3_q, Rd4_q;
  wire [3:0] ex_1_aluctrl;
  wire [5:0] Imm_q;
  wire [11:0] adder_1_out, multiplexer_1_out, multiplexer_2_out, next_pc_1_trgt_addr, NPC2_q, NPC_q, PC_q;
  wire [14:0] main_ctrl_1_ctrl_out, multiplexer_5_out;
  wire [15:0] A_q, alu_1_r, ALUout_q, B_q, bit_extender_1_out, D_q, Instruction2_q, Instruction_q, JAL_R7_q,
       LUI_q, multiplexer_3_out, multiplexer_6_out, multiplexer_7_out, multiplexer_8_out, multiplexer_9_out,
       multiplexer_10_out, next_pc_1_jal_r7, ram_1_dout, register_file_1_bus_a, register_file_1_bus_b,
       rom_1_data, WB_Data_q;

  Multiplexer #(.width(12)) multiplexer_1 (
    .in0(adder_1_out), .in1(next_pc_1_trgt_addr), .out(multiplexer_1_out), .sel(next_pc_1_pcsrc));
  Register #(.width(12)) PC (.D(multiplexer_1_out), .en(not_1_out), .Q(PC_q), .clk(clock_1_out));  // open: clr
  Clock clock_1 (.out(clock_1_out));
  Adder #(.width(12)) adder_1 (.a(12'h1), .b(PC_q), .out(adder_1_out));  // open: cin, cout
  ROM #(.addrWidth(12), .dataWidth(16)) rom_1 (.addr(PC_q), .data(rom_1_data));
  Multiplexer #(.width(12)) multiplexer_2 (
    .in0(PC_q), .in1({12{1'b0}}), .out(multiplexer_2_out), .sel(next_pc_1_pcsrc));
  Multiplexer #(.width(16)) multiplexer_3 (
    .in0(rom_1_data), .in1({16{1'b0}}), .out(multiplexer_3_out), .sel(next_pc_1_pcsrc));
  not not_1 (not_1_out, hazard_detect_n_forward_1_stall);
  Register #(.width(12)) NPC (.D(multiplexer_2_out), .Q(NPC_q), .clk(clock_1_out));  // open: en, clr
  Register #(.width(16)) Instruction (
    .D(multiplexer_3_out), .en(not_1_out), .Q(Instruction_q), .clk(clock_1_out));  // open: clr
  Multiplexer #(.select(2), .width(3)) multiplexer_4 (
    .in0(Instruction_q[8:6]), .in1(Instruction_q[5:3]), .in2(3'b111), .in3(3'b001), .out(multiplexer_4_out),
    .sel(main_ctrl_1_regdst));
  Main_Ctrl main_ctrl_1 (.Inst(Instruction_q), .RegDst(main_ctrl_1_regdst), .Ctrl_Out(main_ctrl_1_ctrl_out));
  Register_File register_file_1 (
    .RegWrite(RegWrite_q), .RW(Rd4_q), .Bus_W(WB_Data_q), .clk(clock_1_out), .RA(Instruction_q[11:9]),
    .RB(Instruction_q[8:6]), .Bus_B(register_file_1_bus_b), .Bus_A(register_file_1_bus_a));
  or or_1 (or_1_out, next_pc_1_pcsrc, hazard_detect_n_forward_1_stall);
  Multiplexer #(.width(15)) multiplexer_5 (
    .in0(main_ctrl_1_ctrl_out), .in1({15{1'b0}}), .out(multiplexer_5_out), .sel(or_1_out));
  Multiplexer #(.select(2), .width(16)) multiplexer_6 (
    .in0(register_file_1_bus_a), .in1(multiplexer_9_out), .in2(multiplexer_10_out), .in3(WB_Data_q),
    .out(multiplexer_6_out), .sel(hazard_detect_n_forward_1_forwarda));
  Multiplexer #(.select(2), .width(16)) multiplexer_7 (
    .in0(register_file_1_bus_b), .in1(multiplexer_9_out), .in2(multiplexer_10_out), .in3(WB_Data_q),
    .out(multiplexer_7_out), .sel(hazard_detect_n_forward_1_forwardb));
  Hazard_Detect_n_Forward hazard_detect_n_forward_1 (
    .EX_MemRead(ex_1_memread), .WB_RW(RegWrite_q), .MEM_RW(mem_1_regwrite), .EX_RW(ex_1_regwrite),
    .Rd4(Rd4_q), .Rd3(Rd3_q), .Rd2(Rd2_q), .Rs(Instruction_q[11:9]), .Rt(Instruction_q[8:6]),
    .Stall(hazard_detect_n_forward_1_stall), .ForwardA(hazard_detect_n_forward_1_forwarda),
    .ForwardB(hazard_detect_n_forward_1_forwardb));
  Register #(.width(16)) Instruction2 (.D(Instruction_q), .Q(Instruction2_q), .clk(clock_1_out));  // open: en, clr
  Register #(.width(12)) NPC2 (.D(NPC_q), .Q(NPC2_q), .clk(clock_1_out));  // open: en, clr
  Register #(.width(6)) Imm (.D(Instruction_q[5:0]), .Q(Imm_q), .clk(clock_1_out));  // open: en, clr
  Register #(.width(16)) A (.D(multiplexer_6_out), .Q(A_q), .clk(clock_1_out));  // open: en, clr
  Register #(.width(16)) B (.D(multiplexer_7_out), .Q(B_q), .clk(clock_1_out));  // open: en, clr
  Register #(.width(3)) Rd2 (.D(multiplexer_4_out), .Q(Rd2_q), .clk(clock_1_out));  // open: en, clr
  EX ex_1 (
    .Ctrl_In(multiplexer_5_out), .Clk(clock_1_out), .toReg(ex_1_toreg), .RegWrite(ex_1_regwrite),
    .ExtOp(ex_1_extop), .ALUSrc(ex_1_alusrc), .ALUCtrl(ex_1_aluctrl), .JR(ex_1_jr), .J(ex_1_j),
    .Bne(ex_1_bne), .Beq(ex_1_beq), .MemRead(ex_1_memread), .MemWrite(ex_1_memwrite));
  assign bit_extender_1_out = {{10{ex_1_extop}}, Imm_q};  // Bit_Extender bit_extender_1
  Multiplexer #(.width(16)) multiplexer_8 (
    .in0(B_q), .in1(bit_extender_1_out), .out(multiplexer_8_out), .sel(ex_1_alusrc));
  Multiplexer #(.width(16)) multiplexer_9 (
    .in0(alu_1_r), .in1({Instruction2_q[11:0], 4'b0000}), .out(multiplexer_9_out), .sel(and_1_out));
  and and_1 (and_1_out, ex_1_toreg[1], ~ex_1_toreg[0]);  // AND_Gate
  Next_PC next_pc_1 (
    .PC(NPC2_q), .curr_instr(Instruction2_q), .Rs(A_q), .Beq(ex_1_beq), .Bne(ex_1_bne),
    .Zero(alu_1_zero_output), .J(ex_1_j), .JR(ex_1_jr), .PCSrc(next_pc_1_pcsrc), .JAL_R7(next_pc_1_jal_r7),
    .Trgt_Addr(next_pc_1_trgt_addr));
  ALU alu_1 (.Rs(A_q), .Rt(multiplexer_8_out), .ALUCtrl(ex_1_aluctrl), .Zero_Output(alu_1_zero_output), .R(alu_1_r));
  Register #(.width(16)) LUI (.D({Instruction2_q[11:0], 4'b0000}), .Q(LUI_q), .clk(clock_1_out));  // open: en, clr
  Register #(.width(16)) JAL_R7 (.D(next_pc_1_jal_r7), .Q(JAL_R7_q), .clk(clock_1_out));  // open: en, clr
  Register #(.width(16)) ALUout (.D(alu_1_r), .Q(ALUout_q), .clk(clock_1_out));  // open: en, clr
  Register #(.width(16)) D (.D(B_q), .Q(D_q), .clk(clock_1_out));  // open: en, clr
  Register #(.width(3)) Rd3 (.D(Rd2_q), .Q(Rd3_q), .clk(clock_1_out));  // open: en, clr
  MEM mem_1 (
    .Clk(clock_1_out), .MemRead_in(ex_1_memread), .MemWrite_in(ex_1_memwrite), .toReg_in(ex_1_toreg),
    .RegWrite_in(ex_1_regwrite), .MemRead(mem_1_memread), .MemWrite(mem_1_memwrite), .toReg(mem_1_toreg),
    .RegWrite(mem_1_regwrite));
  RAM #(.addrWidth(12), .dataWidth(16), .trigger("falling")) ram_1 (
    .addr(ALUout_q[11:0]), .we(mem_1_memwrite), .oe(mem_1_memread), .clk(clock_1_out), .din(D_q),
    .dout(ram_1_dout));
  Multiplexer #(.select(2), .width(16)) multiplexer_10 (
    .in0(ALUout_q), .in1(ram_1_dout), .in2(LUI_q), .in3(JAL_R7_q), .out(multiplexer_10_out), .sel(mem_1_toreg));
  Register #(.width(16)) WB_Data (.D(multiplexer_10_out), .Q(WB_Data_q), .clk(clock_1_out));  // open: en, clr
  Register #(.width(3)) Rd4 (.D(Rd3_q), .Q(Rd4_q), .clk(clock_1_out));  // open: en, clr
  Register #(.width(1)) RegWrite (.D(mem_1_regwrite), .Q(RegWrite_q), .clk(clock_1_out));  // open: en, clr

  // Notes on the sheet:
  //   contents of rom_1 (hex, n*v repeats v):
  //   5046 508a 2a0 869 2b4 7181 2b5 7182 2b6 7183 7140 6180 c78 9f02 505f bf42 509f c014 50df 9002 50cc
  //   9000
endmodule

module Barrel_Shifter (
  input  [2:0] func,
  input  [15:0] shifter_in,
  input  [3:0] shamt,
  output [15:0] shifter_out
);

  wire not_1_out;
  wire [1:0] bit_extender_3_out;
  wire [3:0] bit_extender_2_out;
  wire [7:0] bit_extender_1_out;
  wire [15:0] multiplexer_1_out, multiplexer_3_out, multiplexer_5_out, multiplexer_7_out, multiplexer_8_out;
  wire [15:8] multiplexer_2_out;
  wire [15:12] multiplexer_4_out;
  wire [15:14] multiplexer_6_out;
  wire [15:15] multiplexer_9_out;

  not not_1 (not_1_out, func[1]);
  Multiplexer #(.width(16)) multiplexer_1 (
    .in0(shifter_in),
    .in1({shifter_in[0], shifter_in[1], shifter_in[2], shifter_in[3], shifter_in[4], shifter_in[5], shifter_in[6], shifter_in[7], shifter_in[8], shifter_in[9], shifter_in[10], shifter_in[11], shifter_in[12], shifter_in[13], shifter_in[14], shifter_in[15]}),
    .out(multiplexer_1_out), .sel(not_1_out));
  Multiplexer #(.select(2), .width(8)) multiplexer_2 (
    .in0({8{1'b0}}), .in1(multiplexer_1_out[7:0]), .in2({8{1'b0}}), .in3(bit_extender_1_out),
    .out(multiplexer_2_out));  // open: sel
  Multiplexer #(.width(16)) multiplexer_3 (
    .in0(multiplexer_1_out), .in1({multiplexer_2_out, multiplexer_1_out[15:8]}), .out(multiplexer_3_out),
    .sel(shamt[3]));
  assign bit_extender_1_out = {{7{shifter_in[15]}}, shifter_in[15]};  // Bit_Extender bit_extender_1
  Multiplexer #(.select(2), .width(4)) multiplexer_4 (
    .in0(4'b0000), .in1(multiplexer_3_out[3:0]), .in2(4'b0000), .in3(bit_extender_2_out),
    .out(multiplexer_4_out));  // open: sel
  Multiplexer #(.width(16)) multiplexer_5 (
    .in0(multiplexer_3_out), .in1({multiplexer_4_out, multiplexer_3_out[15:4]}), .out(multiplexer_5_out),
    .sel(shamt[2]));
  assign bit_extender_2_out = {{3{shifter_in[15]}}, shifter_in[15]};  // Bit_Extender bit_extender_2
  assign bit_extender_3_out = {{1{shifter_in[15]}}, shifter_in[15]};  // Bit_Extender bit_extender_3
  Multiplexer #(.select(2), .width(2)) multiplexer_6 (
    .in0(2'b00), .in1(multiplexer_5_out[1:0]), .in2(2'b00), .in3(bit_extender_3_out), .out(multiplexer_6_out));  // open: sel
  Multiplexer #(.width(16)) multiplexer_7 (
    .in0(multiplexer_5_out), .in1({multiplexer_6_out, multiplexer_5_out[15:2]}), .out(multiplexer_7_out),
    .sel(shamt[1]));
  Multiplexer #(.width(16)) multiplexer_8 (
    .in0(multiplexer_7_out), .in1({multiplexer_9_out[15], multiplexer_7_out[15:1]}), .out(multiplexer_8_out),
    .sel(shamt[0]));
  Multiplexer #(.select(2)) multiplexer_9 (
    .in0(1'b0), .in1(multiplexer_7_out[0]), .in2(1'b0), .in3(shifter_in[15]), .out(multiplexer_9_out[15]));  // open: sel
  Multiplexer #(.width(16)) multiplexer_10 (
    .in0(multiplexer_8_out),
    .in1({multiplexer_8_out[0], multiplexer_8_out[1], multiplexer_8_out[2], multiplexer_8_out[3], multiplexer_8_out[4], multiplexer_8_out[5], multiplexer_8_out[6], multiplexer_8_out[7], multiplexer_8_out[8], multiplexer_8_out[9], multiplexer_8_out[10], multiplexer_8_out[11], multiplexer_8_out[12], multiplexer_8_out[13], multiplexer_8_out[14], multiplexer_8_out[15]}),
    .out(shifter_out), .sel(not_1_out));
endmodule

module ALU (
  input  [15:0] Rs,
  input  [15:0] Rt,
  input  [3:0] ALUCtrl,
  output [15:0] R,
  output Zero_Output
);

  wire adder_1_cout, and_1_out, and_3_out, not_1_out, not_2_out, or_1_out, or_2_out, xnor_1_out, xor_3_out,
       xor_4_out, xor_5_out;
  wire [15:0] adder_1_out, and_2_out, barrel_shifter_1_shifter_out, bit_extender_1_out, bit_extender_2_out,
       bit_extender_3_out, multiplexer_1_out, not_3_out, or_3_out, xor_1_out, xor_2_out;

  or or_1 (or_1_out, ALUCtrl[0], ALUCtrl[1]);
  not not_1 (not_1_out, ALUCtrl[2]);
  assign bit_extender_1_out = {{15{and_1_out}}, and_1_out};  // Bit_Extender bit_extender_1
  and and_1 (and_1_out, or_1_out, not_1_out);
  assign xor_1_out = Rt ^ bit_extender_1_out;  // XOR_Gate xor_1, 16 bits wide
  or or_2 (or_2_out, ALUCtrl[2], ALUCtrl[3]);
  Adder #(.width(16)) adder_1 (.a(Rs), .b(xor_1_out), .out(adder_1_out), .cin(and_1_out), .cout(adder_1_cout));
  xnor xnor_1 (xnor_1_out, Rs[15], xor_1_out[15]);
  assign and_2_out = Rs & xor_1_out;  // AND_Gate and_2, 16 bits wide
  assign or_3_out = Rs | xor_1_out;  // OR_Gate or_3, 16 bits wide
  assign xor_2_out = Rs ^ xor_1_out;  // XOR_Gate xor_2, 16 bits wide
  xor xor_3 (xor_3_out, adder_1_out[15], Rs[15]);
  and and_3 (and_3_out, xor_3_out, xnor_1_out);
  not not_2 (not_2_out, adder_1_cout);
  xor xor_4 (xor_4_out, adder_1_cout, and_1_out);
  assign bit_extender_2_out = {{15{1'b0}}, xor_5_out};  // Bit_Extender bit_extender_2
  xor xor_5 (xor_5_out, adder_1_out[15], and_3_out);
  assign bit_extender_3_out = {{15{1'b0}}, not_2_out};  // Bit_Extender bit_extender_3
  assign not_3_out = ~or_3_out;  // NOT_Gate not_3, 16 bits wide
  Barrel_Shifter barrel_shifter_1 (
    .func(ALUCtrl[2:0]), .shifter_in(Rs), .shamt(Rt[3:0]), .shifter_out(barrel_shifter_1_shifter_out));
  Multiplexer #(.select(3), .width(16)) multiplexer_1 (
    .in0(adder_1_out), .in1(adder_1_out), .in2(bit_extender_2_out), .in3(bit_extender_3_out),
    .in4(and_2_out), .in5(or_3_out), .in6(not_3_out), .in7(xor_2_out), .out(multiplexer_1_out),
    .sel(ALUCtrl[2:0]));
  LED CarryOut (.in(xor_4_out));
  LED Overflow (.in(and_3_out));
  LED Negative_Sign (.in(adder_1_out[15]));
  nor nor_1 (Zero_Output, multiplexer_1_out[0], multiplexer_1_out[1], multiplexer_1_out[2], multiplexer_1_out[3], multiplexer_1_out[4], multiplexer_1_out[5], multiplexer_1_out[6], multiplexer_1_out[7], multiplexer_1_out[9], multiplexer_1_out[10], multiplexer_1_out[11], multiplexer_1_out[12], multiplexer_1_out[13], multiplexer_1_out[14], multiplexer_1_out[15], multiplexer_1_out[8]);
  Multiplexer #(.width(16)) multiplexer_2 (
    .in0(barrel_shifter_1_shifter_out), .in1(multiplexer_1_out), .out(R), .sel(or_2_out));
endmodule

module Register_File (
  input  [2:0] RA,
  input  [2:0] RB,
  input  [2:0] RW,
  input  RegWrite,
  input  [15:0] Bus_W,
  input  clk,
  output [15:0] Bus_A,
  output [15:0] Bus_B
);

  wire and_1_out, and_2_out, and_3_out, and_4_out, and_5_out, and_6_out, and_7_out, decoder_1_out1,
       decoder_1_out2, decoder_1_out3, decoder_1_out4, decoder_1_out5, decoder_1_out6, decoder_1_out7,
       decoder_2_out0, decoder_2_out1, decoder_2_out2, decoder_2_out3, decoder_2_out4, decoder_2_out5,
       decoder_2_out6, decoder_2_out7, decoder_3_out0, decoder_3_out1, decoder_3_out2, decoder_3_out3,
       decoder_3_out4, decoder_3_out5, decoder_3_out6, decoder_3_out7;
  wire [15:0] R1_q, R2_q, R3_q, R4_q, R5_q, R6_q, R7_q;

  Decoder #(.enable("false"), .select(3)) decoder_1 (
    .out1(decoder_1_out1), .out2(decoder_1_out2), .out3(decoder_1_out3), .out4(decoder_1_out4),
    .out5(decoder_1_out5), .out6(decoder_1_out6), .out7(decoder_1_out7), .sel(RW));  // open: out0
  and and_1 (and_1_out, decoder_1_out1, RegWrite);
  and and_2 (and_2_out, decoder_1_out2, RegWrite);
  and and_3 (and_3_out, decoder_1_out3, RegWrite);
  and and_4 (and_4_out, decoder_1_out4, RegWrite);
  and and_5 (and_5_out, decoder_1_out5, RegWrite);
  and and_6 (and_6_out, decoder_1_out6, RegWrite);
  and and_7 (and_7_out, decoder_1_out7, RegWrite);
  Register #(.trigger("falling"), .width(16)) R1 (.D(Bus_W), .en(and_1_out), .Q(R1_q), .clk(clk));  // open: clr
  Register #(.trigger("falling"), .width(16)) R2 (.D(Bus_W), .en(and_2_out), .Q(R2_q), .clk(clk));  // open: clr
  Register #(.trigger("falling"), .width(16)) R3 (.D(Bus_W), .en(and_3_out), .Q(R3_q), .clk(clk));  // open: clr
  Register #(.trigger("falling"), .width(16)) R4 (.D(Bus_W), .en(and_4_out), .Q(R4_q), .clk(clk));  // open: clr
  Register #(.trigger("falling"), .width(16)) R5 (.D(Bus_W), .en(and_5_out), .Q(R5_q), .clk(clk));  // open: clr
  Register #(.trigger("falling"), .width(16)) R6 (.D(Bus_W), .en(and_6_out), .Q(R6_q), .clk(clk));  // open: clr
  Register #(.trigger("falling"), .width(16)) R7 (.D(Bus_W), .en(and_7_out), .Q(R7_q), .clk(clk));  // open: clr
  Decoder #(.enable("false"), .select(3)) decoder_2 (
    .out0(decoder_2_out0), .out1(decoder_2_out1), .out2(decoder_2_out2), .out3(decoder_2_out3),
    .out4(decoder_2_out4), .out5(decoder_2_out5), .out6(decoder_2_out6), .out7(decoder_2_out7), .sel(RA));
  assign Bus_A = decoder_2_out0 ? {16{1'b0}} : 16'bz;  // Controlled_Buffer controlled_buffer_1
  assign Bus_A = decoder_2_out1 ? R1_q : 16'bz;  // Controlled_Buffer controlled_buffer_2
  assign Bus_A = decoder_2_out2 ? R2_q : 16'bz;  // Controlled_Buffer controlled_buffer_3
  assign Bus_A = decoder_2_out3 ? R3_q : 16'bz;  // Controlled_Buffer controlled_buffer_4
  assign Bus_A = decoder_2_out4 ? R4_q : 16'bz;  // Controlled_Buffer controlled_buffer_5
  assign Bus_A = decoder_2_out5 ? R5_q : 16'bz;  // Controlled_Buffer controlled_buffer_6
  assign Bus_A = decoder_2_out6 ? R6_q : 16'bz;  // Controlled_Buffer controlled_buffer_7
  assign Bus_A = decoder_2_out7 ? R7_q : 16'bz;  // Controlled_Buffer controlled_buffer_8
  Decoder #(.enable("false"), .select(3)) decoder_3 (
    .out0(decoder_3_out0), .out1(decoder_3_out1), .out2(decoder_3_out2), .out3(decoder_3_out3),
    .out4(decoder_3_out4), .out5(decoder_3_out5), .out6(decoder_3_out6), .out7(decoder_3_out7), .sel(RB));
  assign Bus_B = decoder_3_out0 ? {16{1'b0}} : 16'bz;  // Controlled_Buffer controlled_buffer_9
  assign Bus_B = decoder_3_out1 ? R1_q : 16'bz;  // Controlled_Buffer controlled_buffer_10
  assign Bus_B = decoder_3_out2 ? R2_q : 16'bz;  // Controlled_Buffer controlled_buffer_11
  assign Bus_B = decoder_3_out3 ? R3_q : 16'bz;  // Controlled_Buffer controlled_buffer_12
  assign Bus_B = decoder_3_out4 ? R4_q : 16'bz;  // Controlled_Buffer controlled_buffer_13
  assign Bus_B = decoder_3_out5 ? R5_q : 16'bz;  // Controlled_Buffer controlled_buffer_14
  assign Bus_B = decoder_3_out6 ? R6_q : 16'bz;  // Controlled_Buffer controlled_buffer_15
  assign Bus_B = decoder_3_out7 ? R7_q : 16'bz;  // Controlled_Buffer controlled_buffer_16
endmodule

module Next_PC (
  input  [11:0] PC,
  input  [15:0] curr_instr,
  input  [15:0] Rs,
  input  Beq,
  input  Bne,
  input  Zero,
  input  J,
  input  JR,
  output PCSrc,
  output [15:0] JAL_R7,
  output [11:0] Trgt_Addr
);

  wire and_1_out, and_2_out, or_3_out;
  wire [1:0] or_2_out;
  wire [11:0] adder_1_out, adder_2_out, bit_extender_1_out;

  Adder #(.width(12)) adder_1 (.a(12'h1), .b(PC), .out(adder_1_out));  // open: cin, cout
  assign bit_extender_1_out = {{6{curr_instr[5]}}, curr_instr[5:0]};  // Bit_Extender bit_extender_1
  assign JAL_R7 = {{4{1'b0}}, adder_1_out};  // Bit_Extender bit_extender_2
  Adder #(.width(12)) adder_2 (.a(PC), .b(bit_extender_1_out), .out(adder_2_out));  // open: cin, cout
  Multiplexer #(.select(2), .width(12)) multiplexer_1 (
    .in1(adder_2_out), .in2(curr_instr[11:0]), .in3(Rs[11:0]), .out(Trgt_Addr), .sel(or_2_out));  // open: in0
  or or_1 (or_2_out[1], J, JR);
  or or_2 (or_2_out[0], JR, or_3_out);
  or or_3 (or_3_out, and_1_out, and_2_out);
  and and_1 (and_1_out, ~Zero, Bne);  // AND_Gate
  and and_2 (and_2_out, Zero, Beq);
  or or_4 (PCSrc, or_2_out[1], or_2_out[0]);
endmodule

module Main_Ctrl (
  input  [15:0] Inst,
  output [14:0] Ctrl_Out,
  output [1:0] RegDst
);

  wire ABCnD_out, ABD_out, ADn_out, AnBn_out, AnCn_out, BC_out, BCn_out, BnCor_out, BnDn_out, CD_out,
       CDn_out, or_1_out;
  wire [1:0] or_3_out;

  and and_1 (Ctrl_Out[14], ~Ctrl_Out[6], or_1_out);  // AND_Gate
  and and_2 (Ctrl_Out[0], Inst[5], BnCor_out);
  or or_1 (or_1_out, AnCn_out, ABD_out, BnDn_out, CDn_out);
  or BnCor (BnCor_out, ~Inst[14], Inst[13]);  // OR_Gate
  and JR_Gate (Ctrl_Out[6], Inst[2], Inst[12], ~Inst[14], ~Inst[15]);  // AND_Gate
  and AnCn (AnCn_out, ~Inst[13], ~Inst[15]);  // AND_Gate
  and ABD (ABD_out, Inst[12], Inst[14], Inst[15]);
  and BnDn (BnDn_out, ~Inst[12], ~Inst[14]);  // AND_Gate
  and CDn (CDn_out, Inst[13], ~Inst[12]);  // AND_Gate
  and BC (BC_out, Inst[14], Inst[13]);
  and AD (Ctrl_Out[13], Inst[15], Inst[12]);
  and BCn (BCn_out, ~Inst[13], Inst[14]);  // AND_Gate
  and BCDn (Ctrl_Out[10], ~Inst[12], Inst[13], Inst[14]);  // AND_Gate
  Multiplexer #(.select(2), .width(4)) multiplexer_1 (
    .in0({Inst[12], Inst[2:0]}), .in1(Inst[15:12]), .in2(4'b1000), .in3(4'b1001), .out(Ctrl_Out[5:2]),
    .sel(or_3_out));
  or or_2 (or_3_out[1], BC_out, Ctrl_Out[13]);
  or or_3 (or_3_out[0], Inst[15], BCn_out);
  and ABCnD (ABCnD_out, Inst[15], Inst[14], ~Inst[13], Inst[12]);  // AND_Gate
  and ADn (ADn_out, ~Inst[12], Inst[15]);  // AND_Gate
  and AnBn (AnBn_out, ~Inst[15], ~Inst[14]);  // AND_Gate
  and CD (CD_out, Inst[13], Inst[12]);
  and ABCn (Ctrl_Out[7], Inst[15], BCn_out);
  and ABnCnD (Ctrl_Out[9], Ctrl_Out[13], ~Inst[14], ~Inst[13]);  // AND_Gate
  or or_4 (Ctrl_Out[12], ABCnD_out, Ctrl_Out[10]);
  or orB (Ctrl_Out[1], ADn_out, Inst[14]);
  and AnCD (Ctrl_Out[11], Inst[12], Inst[13], ~Inst[15]);  // AND_Gate
  or RD0 (RegDst[0], AnBn_out, CD_out);
  and BnCD (Ctrl_Out[8], CD_out, ~Inst[14]);  // AND_Gate

  assign RegDst[1] = Ctrl_Out[13];

  // Other names for the same wires on the sheet: ExtOp_T = Ctrl_Out[0]; ALUSrc_T = Ctrl_Out[1];
  //   ALUCtrl_T[3:0] = Ctrl_Out[5:2]; JR_T = Ctrl_Out[6]; J_T = Ctrl_Out[7]; Bne_T = Ctrl_Out[8]; Beq_T = Ctrl_Out[9];
  //   MemRead_T = Ctrl_Out[10]; MemWrite_T = Ctrl_Out[11]; toReg_T[1:0] = Ctrl_Out[13:12]; RegWrite_T = Ctrl_Out[14]

  // Notes on the sheet:
  //   A B C D
endmodule

module EX (
  input  Clk,
  input  [14:0] Ctrl_In,
  output ExtOp,
  output ALUSrc,
  output [3:0] ALUCtrl,
  output JR,
  output J,
  output Bne,
  output Beq,
  output MemRead,
  output MemWrite,
  output [1:0] toReg,
  output RegWrite
);

  Register #(.width(1)) register_1 (.D(Ctrl_In[0]), .Q(ExtOp), .clk(Clk));  // open: en, clr
  Register #(.width(1)) register_2 (.D(Ctrl_In[1]), .Q(ALUSrc), .clk(Clk));  // open: en, clr
  Register #(.width(4)) register_3 (.D(Ctrl_In[5:2]), .Q(ALUCtrl), .clk(Clk));  // open: en, clr
  Register #(.width(1)) register_4 (.D(Ctrl_In[6]), .Q(JR), .clk(Clk));  // open: en, clr
  Register #(.width(1)) register_5 (.D(Ctrl_In[7]), .Q(J), .clk(Clk));  // open: en, clr
  Register #(.width(1)) register_6 (.D(Ctrl_In[8]), .Q(Bne), .clk(Clk));  // open: en, clr
  Register #(.width(1)) register_7 (.D(Ctrl_In[9]), .Q(Beq), .clk(Clk));  // open: en, clr
  Register #(.width(1)) register_8 (.D(Ctrl_In[10]), .Q(MemRead), .clk(Clk));  // open: en, clr
  Register #(.width(1)) register_9 (.D(Ctrl_In[11]), .Q(MemWrite), .clk(Clk));  // open: en, clr
  Register #(.width(2)) register_10 (.D(Ctrl_In[13:12]), .Q(toReg), .clk(Clk));  // open: en, clr
  Register #(.width(1)) register_11 (.D(Ctrl_In[14]), .Q(RegWrite), .clk(Clk));  // open: en, clr
endmodule

module MEM (
  input  Clk,
  input  MemRead_in,
  input  MemWrite_in,
  input  [1:0] toReg_in,
  input  RegWrite_in,
  output MemRead,
  output MemWrite,
  output [1:0] toReg,
  output RegWrite
);

  Register #(.width(1)) register_1 (.D(MemRead_in), .Q(MemRead), .clk(Clk));  // open: en, clr
  Register #(.width(1)) register_2 (.D(MemWrite_in), .Q(MemWrite), .clk(Clk));  // open: en, clr
  Register #(.width(2)) register_3 (.D(toReg_in), .Q(toReg), .clk(Clk));  // open: en, clr
  Register #(.width(1)) register_4 (.D(RegWrite_in), .Q(RegWrite), .clk(Clk));  // open: en, clr
endmodule

module Hazard_Detect_n_Forward (
  input  WB_RW,
  input  MEM_RW,
  input  EX_RW,
  input  [2:0] Rd4,
  input  [2:0] Rd3,
  input  [2:0] Rd2,
  input  [2:0] Rs,
  input  EX_MemRead,
  input  [2:0] Rt,
  output Stall,
  output [1:0] ForwardA,
  output [1:0] ForwardB
);

  wire A_1_out, A_2_out, A_3_out, B_1_out, B_2_out, B_3_out, comparator_1_eq, comparator_2_eq,
       comparator_3_eq, comparator_4_eq, comparator_5_eq, comparator_6_eq, comparator_7_eq, comparator_8_eq,
       not_1_out, not_2_out, or_1_out;
  wire [1:0] multiplexer_1_out, multiplexer_2_out, multiplexer_3_out, multiplexer_4_out;

  Comparator #(.width(3)) comparator_1 (.a(Rs), .b(3'b000), .eq(comparator_1_eq));  // open: gt, lt
  Comparator #(.width(3)) comparator_2 (.a(Rt), .b(3'b000), .eq(comparator_2_eq));  // open: gt, lt
  not not_1 (not_1_out, comparator_1_eq);
  not not_2 (not_2_out, comparator_2_eq);
  Comparator #(.width(3)) comparator_3 (.a(Rs), .b(Rd2), .eq(comparator_3_eq));  // open: gt, lt
  Comparator #(.width(3)) comparator_4 (.a(Rs), .b(Rd3), .eq(comparator_4_eq));  // open: gt, lt
  Comparator #(.width(3)) comparator_5 (.a(Rs), .b(Rd4), .eq(comparator_5_eq));  // open: gt, lt
  Comparator #(.width(3)) comparator_6 (.a(Rt), .b(Rd2), .eq(comparator_6_eq));  // open: gt, lt
  Comparator #(.width(3)) comparator_7 (.a(Rt), .b(Rd3), .eq(comparator_7_eq));  // open: gt, lt
  Comparator #(.width(3)) comparator_8 (.a(Rt), .b(Rd4), .eq(comparator_8_eq));  // open: gt, lt
  and A_1 (A_1_out, not_1_out, comparator_3_eq, EX_RW);
  and A_2 (A_2_out, not_1_out, comparator_4_eq, MEM_RW);
  and A_3 (A_3_out, not_1_out, comparator_5_eq, WB_RW);
  and B_1 (B_1_out, not_2_out, comparator_6_eq, EX_RW);
  and B_2 (B_2_out, not_2_out, comparator_7_eq, MEM_RW);
  and B_3 (B_3_out, not_2_out, comparator_8_eq, WB_RW);
  Multiplexer #(.width(2)) multiplexer_1 (.in0(2'b00), .in1(2'b11), .out(multiplexer_1_out), .sel(A_3_out));
  Multiplexer #(.width(2)) multiplexer_2 (.in0(2'b00), .in1(2'b11), .out(multiplexer_2_out), .sel(B_3_out));
  Multiplexer #(.width(2)) multiplexer_3 (.in0(multiplexer_1_out), .in1(2'b10), .out(multiplexer_3_out), .sel(A_2_out));
  Multiplexer #(.width(2)) multiplexer_4 (.in0(multiplexer_2_out), .in1(2'b10), .out(multiplexer_4_out), .sel(B_2_out));
  Multiplexer #(.width(2)) multiplexer_5 (.in0(multiplexer_3_out), .in1(2'b01), .out(ForwardA), .sel(A_1_out));
  Multiplexer #(.width(2)) multiplexer_6 (.in0(multiplexer_4_out), .in1(2'b01), .out(ForwardB), .sel(B_1_out));
  or or_1 (or_1_out, A_1_out, B_1_out);
  and and_1 (Stall, EX_MemRead, or_1_out);
endmodule
